# Fritzing sketch Circuit design (saved by Fritzing 0.9.4)
perfboards: 1

parts:
  J3 = Basic Servo
  J4 = Basic Servo
  U1 = ESP32S-HiLetgo [part_number=ESP32S-HiLetgo]  # not connected
  Part1 = 16-Channel 12-bit PCA9685 PWM/Servo Driver
  Part3 = GY-VL53L0XV2 Laser Ranger Module  # not connected
  Part4 = GY-VL53L0XV2 Laser Ranger Module  # not connected
  Part5 = GY-VL53L0XV2 Laser Ranger Module  # not connected
  Part6 = GY-VL53L0XV2 Laser Ranger Module  # not connected
  Part7 = GY-VL53L0XV2 Laser Ranger Module  # not connected
  Part8 = GY-VL53L0XV2 Laser Ranger Module  # not connected
  J16 = Basic Servo
  J17 = Basic Servo
  J18 = Basic Servo
  J19 = Basic Servo
  J20 = Basic Servo
  J21 = Basic Servo
  J22 = Basic Servo
  J23 = Basic Servo
  J24 = Basic Servo
  J25 = Basic Servo  # not connected
  U6 = 7-SEGMENT-4DIGIT [package=7-segment-4digit_longpads_for_pogobed]
  U7 = 7-SEGMENT-4DIGIT [package=7-segment-4digit_longpads_for_pogobed]
  S2 = Square Pushbutton
  IC2 = Voltage Regulator LM1117 [package=sot223]
  IC3 = Voltage Regulator LM1117 [package=sot223]
  IC4 = Voltage Regulator LM1117 [package=sot223]
  S1 = Square Pushbutton
  IC7 = Voltage Regulator LM1117 [package=sot223]
  IC8 = Voltage Regulator LM1117 [package=sot223]
  VCC14 = Battery
  U8 = 7-SEGMENT-4DIGIT [package=7-segment-4digit_longpads_for_pogobed]
  U9 = 7-SEGMENT-4DIGIT [package=7-segment-4digit_longpads_for_pogobed]
  U10 = 7-SEGMENT-4DIGIT [package=7-segment-4digit_longpads_for_pogobed]
  C1 = Electrolytic Capacitor [capacitance=100µF package="200 mil [THT, electrolytic]"]  # not connected
  VCC15 = Battery
  VCC16 = Battery
  VCC17 = Battery
  VCC18 = Battery

nets:
  N1: J3.pulse, Part1.1
  N2: J4.gnd, IC8.ADJ
  VCC: J4.vcc, J17.vcc, J23.vcc, J24.vcc, U6.13, IC2.OUT, IC3.OUT, S1.leg1, IC7.OUT, IC8.OUT, U8.13, U9.13, U10.13
  N3: J4.pulse, Part1.2
  N4: Part1.0, J16.pulse
  N5: Part1.4, J21.pulse
  N6: Part1.8, J19.pulse
  N7: Part1.9, J18.pulse
  N8: Part1.10, J17.pulse
  N9: Part1.12, J20.pulse
  N10: Part1.13, J22.pulse
  N11: Part1.14, J24.pulse
  N12: J17.gnd, IC2.ADJ
  N13: J23.gnd, IC7.ADJ
  N14: J24.gnd, IC3.ADJ
  N15: U6.9, U6.11, IC2.IN, VCC15.+
  N16: U7.9, U7.11, S2.leg1, IC4.ADJ
  N17: U7.13, IC4.OUT, VCC14.-
  N18: S2.leg0, VCC14.+
  N19: IC3.IN, U9.9, U9.11, VCC17.+
  N20: S1.leg0, VCC15.-, VCC16.-, VCC17.-, VCC18.-
  N21: IC7.IN, U8.9, U8.11, VCC18.+
  N22: IC8.IN, U10.9, U10.11, VCC16.+

custom parts:
  ESP32S-HiLetgo: HiLetgo ESP-WROOM-32 ESP32 ESP-32S Development Board 2.4GHz Dual-Mode WiFi + Bluetooth Dual Cores Microcontroller The ESP32 integrated with Antenna switches, RF Balun, power amplifiers, low-noise amplifiers, filters, and management modules, and the entire solution occupies the least area of PCB. 2.4 GHz Wi-Fi plus Bluetooth dual-mode chip, with TSMC Ultra-low power consumption 40nm technology,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
  16-Channel 12-bit PCA9685 PWM/Servo Driver: The Adafruit 16-Channel 12-bit PWM/Servo Driver will drive up to 16 servos over I2C with only 2 pins. The on-board PCA9685 PWM controller will drive all 16 channels simultaneously with no additional processing overhead. What's more, you can chain up to 62 of them to control up to 992 servos - all with the same 2 pins
  GY-VL53L0XV2 Laser Ranger Module: The GY-VL53L0XV2 is based on the VL53L0X from ST Microelectronics, a time-of-flight ranging system integrated into a compact module.
